# Fritzing sketch A06_Grove_PushButton_LED13 (saved by Fritzing 0.9.9b)

parts:
  Part1 = Arduino Nano (Rev3.0) (ICSP)
  Grove1 = Grove Button

nets:
  GND: Part1.GND, Grove1.GND
  N1: Part1.D8, Grove1.SIG
  5V: Part1.5V, Grove1.VCC
